# Fritzing sketch 電路圖 (saved by Fritzing 0.9.3b)
breadboards: 1

parts:
  U1 = TL431 [package="TO92 (Two)"]
  R1 = Resistor [tolerance=±5% resistance=10k package="2010 [SMD]"]
  R2 = Resistor [tolerance=±5% resistance=10k package="2010 [SMD]"]
  C1 = Electrolytic Capacitor [capacitance=1µF package="100 mil [THT, electrolytic]"]
  C2 = Ceramic Capacitor [capacitance=100nF package="100 mil [THT, multilayer]"]
  U2 = attiny85 [package=dip]
  元件1 = TM1637
  R5 = Resistor [tolerance=±5% resistance=10k package="2010 [SMD]"]
  R10 = Resistor [tolerance=±5% resistance=330 package="2010 [SMD]"]
  R11 = Resistor [tolerance=±5% resistance=1k package="2010 [SMD]"]
  Q2 = MOSFET-NCHANNEL [package=to220v]
  R12 = Rotary Potentiometer (Large) [maximum_resistance=100kΩ package=THT]
  Q3 = NPN-Transistor [package="TO92 [THT]"]
  R13 = Resistor [tolerance=±5% resistance=4.7k package="2010 [SMD]"]
  U4 = Transformer [package=transformer]
  R14 = Resistor [tolerance=±5% resistance=10k package="2010 [SMD]"]

nets:
  N1: U1.1, R1.Pin_0, R2.Pin_0
  N2: U1.2, R2.Pin_1, C1.-, C2.0, U2.Pin_4, 元件1.VCC, R5.Pin_1, R12.leg1, Q3.C, U4.3, R14.Pin_0
  N3: U1.3, R10.Pin_0, Q2.G
  N4: R1.Pin_1, C1.+, C2.1, U2.Pin_8, 元件1.GND, Q2.S
  N5: U2.Pin_2, R12.wiper
  N6: U2.Pin_3, R5.Pin_0, R11.Pin_0
  N7: U2.Pin_6, 元件1.DIO
  N8: U2.Pin_7, 元件1.CLK
  N9: R10.Pin_1, Q2.D, R13.Pin_0
  N10: R11.Pin_1, Q3.E, R14.Pin_1
  N11: Q3.B, R13.Pin_1, U4.4

notes:
  12V
  接地
  ATTiny85 轉速訊號產生器
  By 羽山秋人 https://3wa.tw
  2026-10-13
  TL431 RAK
  TIP41C GDS
  10KΩ
  10KΩ
  330Ω
  470㎌/25V
  0.1㎌
  ATTiny85
  VR 10KΩ
  TM1637
  1KΩ
  10KΩ
  10KΩ
  4.7KΩ
  NPN 2SC1815 BCE
  小型變壓器
  ST-20(600:1K)
  轉速訊號

custom parts:
  TL431: 2% accuracy adjustable precision shunt regulator
  TM1637: A 4 7-seg display
